# Fritzing sketch Circuit sketch (saved by Fritzing 0.9.3b)
breadboards: 1

parts:
  LM35-Temperature_sensor = LM35 Temperature Sensor [package="TO92 [THT]"]
  Part1 = Arduino Uno (Rev3) - ICSP
  Button = Pushbutton [package="[THT]"]
  LED1 = LED - 5mm [color="Red (633nm)" package="5 mm [THT]"]
  R1 = Resistor [tolerance=±5% resistance=220 package="1206 [SMD]"]
  R2 = Resistor [tolerance=±5% resistance=10k package="2512 [SMD]"]
  DHT11-Humidity_sensor = DHT11 Humitidy and Temperature Sensor (3 pins)

nets:
  N1: LM35-Temperature_sensor.+Vs, Part1.5V, Button.Pin_3, Button.Pin_4, DHT11-Humidity_sensor.Signal
  N2: LM35-Temperature_sensor.Vout, Part1.A0
  GND: LM35-Temperature_sensor.GND, Part1.GND, R1.Pin_1, R2.Pin_1, DHT11-Humidity_sensor.Gnd
  N3: Part1.D2, Button.Pin_1, Button.Pin_2, R2.Pin_0
  N4: Part1.D4, LED1.anode
  N5: Part1.D7, DHT11-Humidity_sensor.Plus
  N6: LED1.cathode, R1.Pin_0

custom parts:
  DHT11 Humitidy and Temperature Sensor (3 pins): DHT11 Humidity and Temperature Sensor (3 pins).
